# Fritzing sketch arduino_system (saved by Fritzing 0.8.7b)

parts:
  Part1 = Arduino Uno (Rev3)
  LED1 = LED - 5mm [color="Red (633nm)" package="5 mm [THT]"]
  J1 = Basic Servo

nets:
  N1: Part1.D10_PWM/SS, J1.pulse
  N2: Part1.D11_PWM/MOSI, LED1.anode
  GND: Part1.GND, LED1.cathode, J1.gnd
  5V: Part1.5V, J1.vcc
